# Fritzing sketch Ver_V01 (saved by Fritzing 0.9.3b)
perfboards: 1

parts:
  U1 = Vibration Motor- ROB-08449 [package=vibe-motor-10mm]
  IC1 = ULN2003A [package="SO16 [SMD]"]
  J1 = Basic Force Sensing Resistor (FSR) [package=THT]
  J2 = Basic Force Sensing Resistor (FSR) [package=THT]
  J3 = Basic Force Sensing Resistor (FSR) [package=THT]
  J4 = Basic Force Sensing Resistor (FSR) [package=THT]
  R1 = Basic Flex Resistor
  R2 = Resistor [tolerance=±5% resistance=3.3k package="0603 [SMD]"]
  R3 = Resistor [tolerance=±5% resistance=3.3k package="0603 [SMD]"]
  R4 = Resistor [tolerance=±5% resistance=3.3k package="0603 [SMD]"]
  R5 = Resistor [tolerance=±5% resistance=3.3k package="0603 [SMD]"]
  R6 = Resistor [tolerance=±5% resistance=22k package="0603 [SMD]"]
  Teensy_3_1 = Teensy 3.1
  U2 = LIPO-110mAh [package=lipo-110]  # not connected

nets:
  N1: U1.+, IC1.Out_7
  N2: U1.-, IC1.COM_-_Common, Teensy_3_1.Vin
  N3: IC1.In_7, Teensy_3_1.A7/D21
  N4: IC1.0V, R2.Pin_1
  N5: J1.pin_0, Teensy_3_1.3V3
  N6: J1.pin_1, R2.Pin_0, Teensy_3_1.A0/D14
  N7: J2.pin_1, R3.Pin_0, Teensy_3_1.A1/D15
  N8: J3.pin_1, R4.Pin_0, Teensy_3_1.A2/D16
  N9: J4.pin_1, R5.Pin_0, Teensy_3_1.A3/D17
  N10: R1.Pin_2, R6.Pin_0, Teensy_3_1.A6/D20
